# Fritzing sketch Potentiometer1 (saved by Fritzing 0.9.4)
breadboards: 1

parts:
  Argon1 = Particle Argon
  R1 = Trimmer Potentiometer [maximum_resistance=10kΩ package=THT]
  R2 = Resistor [tolerance=±5% resistance=220 package="0603 [SMD]"]
  R3 = Resistor [tolerance=±5% resistance=220 package="0603 [SMD]"]

nets:
  N1: Argon1.3.3V, R1.leg2, R2.Pin_1
  N2: Argon1.GND, R1.leg1, R3.Pin_0
  N3: Argon1.A3, R2.Pin_0, R3.Pin_1
  N4: Argon1.A5, R1.wiper

custom parts:
  Particle Argon: The Argon is a powerful Wi-Fi enabled development board that can act as either a standalone Wi-Fi endpoint or Wi-Fi enabled gateway for Particle Mesh networks. It is based on the Nordic nRF52840 and has built-in battery charging circuitry so it’s easy to connect a Li-Po and deploy your local network in minutes. The Argon is great for connecting existing projects to the Particle Device Cloud or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
