# Fritzing sketch Quiz2 (saved by Fritzing 0.9.4)
circuit board: 8.46667cm x 5.64444cm
breadboards: 1

parts:
  Argon1 = Particle Argon
  R1 = Trimmer Potentiometer [maximum_resistance=10kΩ package=THT]
  R2 = Resistor [tolerance=±5% resistance=220 package="0805 [SMD]"]
  R3 = Resistor [tolerance=±5% resistance=220 package="0805 [SMD]"]
  R4 = Resistor [tolerance=±5% resistance=220 package="0805 [SMD]"]
  LED2 = LED - 5mm [color="Green (560nm)" package="5 mm [THT]"]
  LED3 = LED - 5mm [color="Blue (470nm)" package="5 mm [THT]"]
  S2 = Pushbutton [package="[THT]"]

nets:
  N1: Argon1.3.3V, R1.leg2, S2.Pin_3, S2.Pin_4
  N2: Argon1.GND, R1.leg1, R2.Pin_1, R3.Pin_1, R4.Pin_1
  N3: Argon1.A5, R1.wiper
  N4: Argon1.D2, R2.Pin_0, S2.Pin_1, S2.Pin_2
  N5: Argon1.D3, LED2.anode
  N6: Argon1.D4, LED3.anode
  N7: R3.Pin_0, LED2.cathode
  N8: R4.Pin_0, LED3.cathode

custom parts:
  Particle Argon: The Argon is a powerful Wi-Fi enabled development board that can act as either a standalone Wi-Fi endpoint or Wi-Fi enabled gateway for Particle Mesh networks. It is based on the Nordic nRF52840 and has built-in battery charging circuitry so it’s easy to connect a Li-Po and deploy your local network in minutes. The Argon is great for connecting existing projects to the Particle Device Cloud or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
  Pushbutton: A generic pushbutton.
