# Fritzing sketch Simon (saved by Fritzing 0.9.4)
circuit board: 8.46667cm x 5.64444cm
breadboards: 1

parts:
  Argon1 = Particle Argon
  LED1 = LED - 5mm [color="Blue (430nm)" package="5 mm [THT]"]
  LED2 = LED - 5mm [color="Yellow (595nm)" package="5 mm [THT]"]
  LED3 = LED - 5mm [color="Green (555nm)" package="5 mm [THT]"]
  LED4 = LED - 5mm [color="Red (633nm)" package="5 mm [THT]"]
  R1 = Resistor [tolerance=±5% resistance=220 package="2010 [SMD]"]
  R2 = Resistor [tolerance=±5% resistance=220 package="2010 [SMD]"]
  R3 = Resistor [tolerance=±5% resistance=220 package="2010 [SMD]"]
  R4 = Resistor [tolerance=±5% resistance=220 package="2010 [SMD]"]
  S1 = Pushbutton [package="[THT]"]
  S2 = Pushbutton [package="[THT]"]
  S3 = Pushbutton [package="[THT]"]
  S4 = Pushbutton [package="[THT]"]

nets:
  N1: Argon1.GND, R1.Pin_1, R2.Pin_1, R3.Pin_1, R4.Pin_1, S1.Pin_3, S1.Pin_4, S2.Pin_3, S2.Pin_4, S3.Pin_3, S3.Pin_4, S4.Pin_3, S4.Pin_4
  N2: Argon1.MO, S4.Pin_1, S4.Pin_2
  N3: Argon1.MI, S3.Pin_1, S3.Pin_2
  N4: Argon1.RX, S2.Pin_1, S2.Pin_2
  N5: Argon1.TX, S1.Pin_1, S1.Pin_2
  N6: Argon1.D2, LED1.anode
  N7: Argon1.D3, LED2.anode
  N8: Argon1.D4, LED3.anode
  N9: Argon1.D5, LED4.anode
  N10: LED1.cathode, R1.Pin_0
  N11: LED2.cathode, R2.Pin_0
  N12: LED3.cathode, R3.Pin_0
  N13: LED4.cathode, R4.Pin_0

custom parts:
  Particle Argon: The Argon is a powerful Wi-Fi enabled development board that can act as either a standalone Wi-Fi endpoint or Wi-Fi enabled gateway for Particle Mesh networks. It is based on the Nordic nRF52840 and has built-in battery charging circuitry so it’s easy to connect a Li-Po and deploy your local network in minutes. The Argon is great for connecting existing projects to the Particle Device Cloud or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
  Pushbutton: A generic pushbutton.
