# Fritzing sketch PedalAmp (saved by Fritzing 0.9.4)
circuit board: 8.46667cm x 5.64444cm
breadboards: 1

parts:
  C1 = Ceramic Capacitor [capacitance=100nF package="100 mil [THT, multilayer]"]
  R1 = Resistor [tolerance=±5% resistance=220 package="0805 [SMD]"]
  Q1 = PNP-Transistor [package="TO92 [THT]"]
  R2 = Resistor [tolerance=±5% resistance=220 package="2010 [SMD]"]
  C2 = Ceramic Capacitor [capacitance=100nF package="200 mil [THT, multilayer]"]
  C3 = Capacitor [package=cap-pth-small-kit]
  R3 = Resistor [tolerance=±5% resistance=220 package="2010 [SMD]"]
  Q2 = PNP-Transistor [package="TO92 [THT]"]
  R4 = Resistor [tolerance=±5% resistance=220 package="2010 [SMD]"]
  R5 = Resistor [tolerance=±5% resistance=220 package="2010 [SMD]"]
  C4 = Capacitor [package=cap-pth-small-kit]
  C5 = Capacitor [package=cap-pth-small-kit]
  C6 = Capacitor [package=cap-pth-small-kit]
  R8 = Resistor [tolerance=±5% resistance=220 package="2010 [SMD]"]
  VCC1 = Battery block 9V
  R6 = Trimmer Potentiometer [maximum_resistance=350k package=THT]
  R7 = Trimmer Potentiometer [maximum_resistance=350k package=THT]
  J1 = BANANA_CONN [package=banana_conn]
  J2 = BANANA_CONN [package=banana_conn]
  J3 = BANANA_CONN [package=banana_conn]
  J4 = BANANA_CONN [package=banana_conn]

nets:
  N1: C1.0, J1.1
  N2: C1.1, R1.Pin_0, Q1.B
  N3: R1.Pin_1, Q1.C, R2.Pin_0, C2.0, C3.1
  N4: Q1.E, Q2.E, C4.2, C5.2, R8.Pin_1, VCC1.-, R7.leg2, J3.1, J4.1
  N5: R2.Pin_1, R4.Pin_0, C5.1, VCC1.+
  N6: C2.1, R6.leg1
  N7: C3.2, R3.Pin_0, Q2.B
  N8: R3.Pin_1, Q2.C, R5.Pin_1, C6.1
  N9: R4.Pin_1, R5.Pin_0, C4.1
  N10: C6.2, R8.Pin_0, R6.leg2
  N11: R6.wiper, R7.leg1
  N12: R7.wiper, J2.1
