# Fritzing sketch Untitled Sketch 2 (saved by Fritzing 0.9.4)
circuit board: 8.46667cm x 5.64444cm
breadboards: 1

parts:
  C1 = Ceramic Capacitor [capacitance=100nF package="100 mil [THT, multilayer]"]
  R1 = Resistor [tolerance=±5% resistance=220 package="0805 [SMD]"]
  Q1 = PNP-Transistor [package="TO92 [THT]"]
  R2 = Resistor [tolerance=±5% resistance=220 package="2010 [SMD]"]
  C2 = Ceramic Capacitor [capacitance=100nF package="200 mil [THT, multilayer]"]
  C3 = Capacitor [package=cap-pth-small-kit]
  R3 = Resistor [tolerance=±5% resistance=220 package="2010 [SMD]"]
  Q2 = PNP-Transistor [package="TO92 [THT]"]
  R4 = Resistor [tolerance=±5% resistance=220 package="2010 [SMD]"]
  R5 = Resistor [tolerance=±5% resistance=220 package="2010 [SMD]"]
  C4 = Capacitor [package=cap-pth-small-kit]
  C5 = Capacitor [package=cap-pth-small-kit]
  C6 = Capacitor [package=cap-pth-small-kit]
  R6 = Rotary Potentiometer (Large) [maximum_resistance=100kΩ package=THT]
  R7 = Rotary Potentiometer (Large) [maximum_resistance=100kΩ package=THT]
  R8 = Resistor [tolerance=±5% resistance=220 package="2010 [SMD]"]
  VCC1 = Battery block 9V

nets:
  N1: C1.1, R1.Pin_0, R1.Pin_1, Q1.B, Q1.C, R2.Pin_0, C2.0, C3.1
  N2: Q1.E, R2.Pin_1, R3.Pin_1, Q2.E, Q2.C, R4.Pin_0, R5.Pin_1, C4.2, C5.1, C5.2, C6.1, C6.2, R6.wiper, R6.leg2, R7.leg1, R7.leg2, R8.Pin_0, R8.Pin_1, VCC1.-, VCC1.+
  N3: C2.1, R6.leg1
  N4: C3.2, R3.Pin_0, Q2.B
  N5: R4.Pin_1, R5.Pin_0, C4.1
